// Logisim project cmc240_lab4.circ as structural Verilog: 1 circuit, main circuit main
module main (
  input  [3:0] A,
  input  [3:0] B,
  input  sub
);

  wire adder_1_cout, and_1_out, SOV, UOV;
  wire [3:0] multiplexer_1_out, not_1_p2, O;

  Multiplexer #(.width(4)) multiplexer_1 (.in0(B), .in1(not_1_p2), .out(multiplexer_1_out), .sel(sub));  // open: en
  // NOT_Gate #(.width(4)) not_1: pin names not known; wires that end beside it: B, not_1_p2
  // Probe on A
  // Probe on B
  // Probe on O
  LED led_1 (.in(UOV));
  Adder #(.width(4)) adder_1 (.a(A), .b(multiplexer_1_out), .out(O), .cin(sub), .cout(adder_1_cout));
  and and_1 (and_1_out, multiplexer_1_out[3], A[3], O[3]);
  // Probe on A
  // Probe on B
  // Probe on O
  LED led_2 (.in(SOV));
  xor xor_1 (UOV, adder_1_cout, sub);
  not not_2 (SOV, and_1_out);
endmodule
