// Logisim project cmc240_lab5.circ as structural Verilog: 1 circuit, main circuit main
module main (
);

  wire Bout, button_1_out, CLK, clock_1_out, subtractor_1_bout;
  wire [15:0] bit_extender_1_out, Dividend_Rem_q, Divisor_q, or_2_out, Quotient_q, shifter_1_out,
       shifter_2_out, subtractor_1_out;

  Clock clock_1 (.out(clock_1_out));
  or or_1 (CLK, clock_1_out, button_1_out);
  Button button_1 (.out(button_1_out));
  Shifter #(.width(16), .shift("lr")) shifter_1 (.in(Divisor_q), .\dist (4'b0001), .out(shifter_1_out));
  Shifter #(.width(16)) shifter_2 (.in(Quotient_q), .\dist (4'b0001), .out(shifter_2_out));
  assign bit_extender_1_out = {{15{1'b0}}, Bout};  // Bit_Extender bit_extender_1
  Register #(.width(16)) Divisor (.D(shifter_1_out), .Q(Divisor_q), .clk(CLK));  // open: en, clr
  assign or_2_out = shifter_2_out | bit_extender_1_out;  // OR_Gate or_2, 16 bits wide
  Register #(.width(16)) Quotient (.D(or_2_out), .Q(Quotient_q), .clk(CLK));  // open: en, clr
  Register #(.width(16)) Dividend_Rem (.D(subtractor_1_out), .en(Bout), .Q(Dividend_Rem_q), .clk(CLK));  // open: clr
  // Probe on Dividend_Rem_q
  Subtractor #(.width(16)) subtractor_1 (
    .a(Dividend_Rem_q), .b(Divisor_q), .out(subtractor_1_out), .bout(subtractor_1_bout));  // open: bin
  not not_1 (Bout, subtractor_1_bout);
  // Probe on Divisor_q
  // Probe on Quotient_q
endmodule
