// Logisim project lab07.circ as structural Verilog: 2 circuits, main circuit main
module main (
  input  [7:0] Input
);

  wire segment_a_1_a, segment_a_1_b, segment_a_1_c, segment_a_1_d, segment_a_1_e, segment_a_1_f,
       segment_a_1_g, segment_a_1_h, segment_a_2_a, segment_a_2_b, segment_a_2_c, segment_a_2_d,
       segment_a_2_e, segment_a_2_f, segment_a_2_g, segment_a_2_h;

  segment_A segment_a_1 (
    .BCD(Input[7:4]), .A(segment_a_1_a), .B(segment_a_1_b), .C(segment_a_1_c), .D(segment_a_1_d),
    .E(segment_a_1_e), .F(segment_a_1_f), .G(segment_a_1_g), .H(segment_a_1_h));
  _7_Segment_Display u_7_segment_display_1 (
    .g(segment_a_1_a), .f(segment_a_1_b), .a(segment_a_1_c), .b(segment_a_1_d), .e(segment_a_1_e),
    .d(segment_a_1_f), .c(segment_a_1_g), .dp(segment_a_1_h));
  segment_A segment_a_2 (
    .BCD(Input[3:0]), .A(segment_a_2_a), .B(segment_a_2_b), .C(segment_a_2_c), .D(segment_a_2_d),
    .E(segment_a_2_e), .F(segment_a_2_f), .G(segment_a_2_g), .H(segment_a_2_h));
  _7_Segment_Display u_7_segment_display_2 (
    .g(segment_a_2_a), .f(segment_a_2_b), .a(segment_a_2_c), .b(segment_a_2_d), .e(segment_a_2_e),
    .d(segment_a_2_f), .c(segment_a_2_g), .dp(segment_a_2_h));
endmodule

module segment_A (
  input  [3:0] BCD,
  output A,
  output B,
  output C,
  output D,
  output E,
  output F,
  output G,
  output H
);

  wire and_1_out, and_2_out, and_3_out, and_4_out, and_5_out, and_6_out, and_7_out, and_8_out, and_9_out,
       and_10_out, and_11_out, and_12_out, and_13_out, and_14_out, and_15_out, and_16_out, and_17_out,
       and_18_out, and_19_out, and_20_out, and_21_out, and_22_out, and_23_out, and_24_out, and_25_out,
       and_26_out, not_1_out, not_2_out, not_3_out, not_4_out, or_1_out, or_2_out;

  not not_1 (not_1_out, BCD[3]);
  not not_2 (not_2_out, BCD[1]);
  not not_3 (not_3_out, BCD[2]);
  not not_4 (not_4_out, BCD[0]);
  and and_1 (and_1_out, not_3_out, BCD[1]);
  and and_2 (and_2_out, BCD[1], not_4_out);
  and and_3 (and_3_out, BCD[2], not_2_out);
  and and_4 (and_4_out, not_4_out, not_2_out);
  and and_5 (and_5_out, BCD[2], not_4_out);
  and and_6 (and_6_out, BCD[2], not_2_out);
  and and_7 (and_7_out, not_3_out, not_4_out);
  and and_8 (and_8_out, BCD[2], BCD[0]);
  and and_9 (and_9_out, BCD[1], not_3_out);
  and and_10 (and_10_out, not_1_out, not_3_out);
  and and_11 (and_11_out, not_2_out, not_3_out);
  and and_12 (and_12_out, not_2_out, not_4_out, not_1_out);
  and and_13 (and_13_out, BCD[0], not_1_out, BCD[1]);
  and and_14 (and_14_out, not_4_out, not_3_out);
  and and_15 (and_15_out, BCD[1], not_4_out);
  and and_16 (and_16_out, BCD[3], BCD[2]);
  and and_17 (and_17_out, BCD[1], BCD[3]);
  and and_18 (and_18_out, BCD[1], not_4_out);
  and and_19 (and_19_out, BCD[1], not_3_out);
  and and_20 (and_20_out, not_4_out, not_3_out);
  and and_21 (and_21_out, BCD[2], not_2_out, BCD[0]);
  and and_22 (and_22_out, not_1_out, BCD[2]);
  and and_23 (and_23_out, not_3_out, not_2_out);
  and and_24 (and_24_out, not_1_out, BCD[0], not_3_out);
  and and_25 (and_25_out, BCD[2], BCD[3]);
  and and_26 (and_26_out, BCD[3], BCD[1]);
  or or_1 (or_1_out, and_1_out, and_2_out);
  or or_2 (or_2_out, and_3_out, BCD[3]);
  or or_3 (A, or_1_out, or_2_out);
  or or_4 (B, BCD[3], and_4_out, and_5_out, and_6_out);
  or or_5 (C, BCD[3], and_7_out, and_8_out, and_9_out);
  or or_6 (D, and_10_out, and_11_out, and_12_out, and_13_out);
  or or_7 (E, and_14_out, and_15_out, and_16_out, and_17_out);
  or or_8 (F, BCD[3], and_18_out, and_19_out, and_20_out, and_21_out);
  or or_9 (G, and_22_out, and_23_out, and_24_out);
  or or_10 (H, and_25_out, and_26_out);
endmodule
